// Logisim project DS_Project_team1.circ as structural Verilog: 12 circuits, main circuit main
module main (
  input  CHILD,
  input  TEEN,
  input  ADULT,
  input  SENIOR,
  input  [3:0] DISTANCE,
  input  TRANSFER,
  input  ROUND_TRIP,
  input  [5:0] in_8,
  input  [5:0] in_9,
  input  \초기화 ,
  output [5:0] Balance
);

  wire \_100원_out , \_500원_out , \_1000원_out , and_1_out, and_2_out, and_3_out, bcd_to_7_segment_1_a,
       bcd_to_7_segment_1_b, bcd_to_7_segment_1_c, bcd_to_7_segment_1_d, bcd_to_7_segment_1_e,
       bcd_to_7_segment_1_f, bcd_to_7_segment_1_g, bcd_to_7_segment_2_a, bcd_to_7_segment_2_b,
       bcd_to_7_segment_2_c, bcd_to_7_segment_2_d, bcd_to_7_segment_2_e, bcd_to_7_segment_2_f,
       bcd_to_7_segment_2_g, bcd_to_7_segment_3_a, bcd_to_7_segment_3_b, bcd_to_7_segment_3_c,
       bcd_to_7_segment_3_d, bcd_to_7_segment_3_e, bcd_to_7_segment_3_f, bcd_to_7_segment_3_g,
       bcd_to_7_segment_4_a, bcd_to_7_segment_4_b, bcd_to_7_segment_4_c, bcd_to_7_segment_4_d,
       bcd_to_7_segment_4_e, bcd_to_7_segment_4_f, bcd_to_7_segment_4_g, bcd_to_7_segment_5_a,
       bcd_to_7_segment_5_b, bcd_to_7_segment_5_c, bcd_to_7_segment_5_d, bcd_to_7_segment_5_e,
       bcd_to_7_segment_5_f, bcd_to_7_segment_5_g, bcd_to_7_segment_6_a, bcd_to_7_segment_6_b,
       bcd_to_7_segment_6_c, bcd_to_7_segment_6_d, bcd_to_7_segment_6_e, bcd_to_7_segment_6_f,
       bcd_to_7_segment_6_g, clock_1_out, INPUT_RESET_out, mod6_counter_1_q0, mod6_counter_1_q1,
       mod6_counter_1_q2, mod6_counter_1_z, mod6_counter_2_q0, mod6_counter_2_q1, mod6_counter_2_q2,
       mod6_counter_2_z, mod10_counter_1_d0_lsb, mod10_counter_1_d1, mod10_counter_1_d2,
       mod10_counter_1_d3_msb, mod10_counter_1_z, mod10_counter_2_d0_lsb, mod10_counter_2_d1,
       mod10_counter_2_d2, mod10_counter_2_d3_msb, mod10_counter_2_z, MoneyInput_moneyinsertcheck,
       MoneyRefund_balance_calculation_complete, n7segmentlogic_1_a, n7segmentlogic_1_b, n7segmentlogic_1_c,
       n7segmentlogic_1_d, n7segmentlogic_1_e, n7segmentlogic_1_f, n7segmentlogic_1_g, n7segmentlogic_2_a,
       n7segmentlogic_2_b, n7segmentlogic_2_c, n7segmentlogic_2_d, n7segmentlogic_2_e, n7segmentlogic_2_f,
       n7segmentlogic_2_g, n7segmentlogic_3_a, n7segmentlogic_3_b, n7segmentlogic_3_c, n7segmentlogic_3_d,
       n7segmentlogic_3_e, n7segmentlogic_3_f, n7segmentlogic_3_g, n7segmentlogic_4_a, n7segmentlogic_4_b,
       n7segmentlogic_4_c, n7segmentlogic_4_d, n7segmentlogic_4_e, n7segmentlogic_4_f, n7segmentlogic_4_g,
       n7segmentlogic_5_a, n7segmentlogic_5_b, n7segmentlogic_5_c, n7segmentlogic_5_d, n7segmentlogic_5_e,
       n7segmentlogic_5_f, n7segmentlogic_5_g, n7segmentlogic_6_a, n7segmentlogic_6_b, n7segmentlogic_6_c,
       n7segmentlogic_6_d, n7segmentlogic_6_e, n7segmentlogic_6_f, n7segmentlogic_6_g, n7segmentlogic_7_a,
       n7segmentlogic_7_b, n7segmentlogic_7_c, n7segmentlogic_7_d, n7segmentlogic_7_e, n7segmentlogic_7_f,
       n7segmentlogic_7_g, n7segmentlogic_8_a, n7segmentlogic_8_b, n7segmentlogic_8_c, n7segmentlogic_8_d,
       n7segmentlogic_8_e, n7segmentlogic_8_f, n7segmentlogic_8_g, n7segmentlogic_9_a, n7segmentlogic_9_b,
       n7segmentlogic_9_c, n7segmentlogic_9_d, n7segmentlogic_9_e, n7segmentlogic_9_f, n7segmentlogic_9_g,
       n7segmentlogic_10_a, n7segmentlogic_10_b, n7segmentlogic_10_c, n7segmentlogic_10_d,
       n7segmentlogic_10_e, n7segmentlogic_10_f, n7segmentlogic_10_g, n7segmentlogic_11_a,
       n7segmentlogic_11_b, n7segmentlogic_11_c, n7segmentlogic_11_d, n7segmentlogic_11_e,
       n7segmentlogic_11_f, n7segmentlogic_11_g, n7segmentlogic_12_a, n7segmentlogic_12_b,
       n7segmentlogic_12_c, n7segmentlogic_12_d, n7segmentlogic_12_e, n7segmentlogic_12_f,
       n7segmentlogic_12_g, n7segmentlogic_13_a, n7segmentlogic_13_b, n7segmentlogic_13_c,
       n7segmentlogic_13_d, n7segmentlogic_13_e, n7segmentlogic_13_f, n7segmentlogic_13_g,
       n7segmentlogic_14_a, n7segmentlogic_14_b, n7segmentlogic_14_c, n7segmentlogic_14_d,
       n7segmentlogic_14_e, n7segmentlogic_14_f, n7segmentlogic_14_g, n12h_counter_1_a0, n12h_counter_1_b0,
       n12h_counter_1_b1, n12h_counter_1_b2, n12h_counter_1_b3, not_1_out, not_2_out, or_1_out, timer_1_out_5;
  wire [5:0] AddCharge_out_3, adder_1_out, divider_1_out, divider_1_rem, divider_2_out, divider_2_rem,
       divider_3_out, divider_3_rem, MoneyInput_amount_inserted, multiplexer_1_out, multiplexer_2_out,
       multiplexer_3_out, multiplier_1_out, register_1_q, SelectAge_out_5, \timer_1__1의_자리 ,
       \timer_1__10의_자리 ;

  _7_Segment_Display u_7_segment_display_1 (
    .g(bcd_to_7_segment_1_g), .f(bcd_to_7_segment_1_f), .a(bcd_to_7_segment_1_a), .b(bcd_to_7_segment_1_b),
    .e(bcd_to_7_segment_1_e), .d(bcd_to_7_segment_1_d), .c(bcd_to_7_segment_1_c));  // open: dp
  BCD_to_7_segment bcd_to_7_segment_1 (
    .MSB_D3(1'b0), .D2(1'b0), .D1(1'b0), .LSB_D0(n12h_counter_1_a0), .A(bcd_to_7_segment_1_a),
    .B(bcd_to_7_segment_1_b), .C(bcd_to_7_segment_1_c), .D(bcd_to_7_segment_1_d), .E(bcd_to_7_segment_1_e),
    .F(bcd_to_7_segment_1_f), .G(bcd_to_7_segment_1_g));
  SelectAge SelectAge (
    .CHILD(CHILD), .TEEN(TEEN), .ADULT(ADULT), .SENIOR(SENIOR), .out_5(SelectAge_out_5));  // open: out_6
  AddCharge AddCharge (.DISTANCES(DISTANCE), .TRANSFER(TRANSFER), .out_3(AddCharge_out_3));  // open: out_4
  _7_Segment_Display u_7_segment_display_2 (
    .g(bcd_to_7_segment_2_g), .f(bcd_to_7_segment_2_f), .a(bcd_to_7_segment_2_a), .b(bcd_to_7_segment_2_b),
    .e(bcd_to_7_segment_2_e), .d(bcd_to_7_segment_2_d), .c(bcd_to_7_segment_2_c));  // open: dp
  BCD_to_7_segment bcd_to_7_segment_2 (
    .MSB_D3(n12h_counter_1_b3), .D2(n12h_counter_1_b2), .D1(n12h_counter_1_b1), .LSB_D0(n12h_counter_1_b0),
    .A(bcd_to_7_segment_2_a), .B(bcd_to_7_segment_2_b), .C(bcd_to_7_segment_2_c), .D(bcd_to_7_segment_2_d),
    .E(bcd_to_7_segment_2_e), .F(bcd_to_7_segment_2_f), .G(bcd_to_7_segment_2_g));
  _12h_counter u_12h_counter_1 (
    .Clk(clock_1_out), .Enable(and_1_out), .Clear(\초기화 ), .A0(n12h_counter_1_a0), .B0(n12h_counter_1_b0),
    .B1(n12h_counter_1_b1), .B2(n12h_counter_1_b2), .B3(n12h_counter_1_b3));
  and and_1 (and_1_out, mod6_counter_1_z, and_2_out);
  Clock clock_1 (.out(clock_1_out));
  BCD_to_7_segment bcd_to_7_segment_3 (
    .MSB_D3(1'b0), .D2(mod6_counter_1_q2), .D1(mod6_counter_1_q1), .LSB_D0(mod6_counter_1_q0),
    .A(bcd_to_7_segment_3_a), .B(bcd_to_7_segment_3_b), .C(bcd_to_7_segment_3_c), .D(bcd_to_7_segment_3_d),
    .E(bcd_to_7_segment_3_e), .F(bcd_to_7_segment_3_f), .G(bcd_to_7_segment_3_g));
  and and_2 (and_2_out, mod10_counter_1_z, and_3_out);
  Adder #(.width(6)) adder_1 (.a(SelectAge_out_5), .b(AddCharge_out_3), .out(adder_1_out));  // open: cin, cout
  Divider #(.width(6)) divider_1 (
    .a(register_1_q), .b(6'b001010), .out(divider_1_out), .rem(divider_1_rem));  // open: upper
  _7_Segment_Display u_7_segment_display_3 (
    .g(n7segmentlogic_1_g), .f(n7segmentlogic_1_f), .a(n7segmentlogic_1_a), .b(n7segmentlogic_1_b),
    .e(n7segmentlogic_1_e), .d(n7segmentlogic_1_d), .c(n7segmentlogic_1_c));  // open: dp
  _7segmentLogic u_7segmentlogic_1 (
    .\숫자 (divider_1_out), .a(n7segmentlogic_1_a), .b(n7segmentlogic_1_b), .c(n7segmentlogic_1_c),
    .d(n7segmentlogic_1_d), .e(n7segmentlogic_1_e), .f(n7segmentlogic_1_f), .g(n7segmentlogic_1_g));
  _7_Segment_Display u_7_segment_display_4 (
    .g(bcd_to_7_segment_3_g), .f(bcd_to_7_segment_3_f), .a(bcd_to_7_segment_3_a), .b(bcd_to_7_segment_3_b),
    .e(bcd_to_7_segment_3_e), .d(bcd_to_7_segment_3_d), .c(bcd_to_7_segment_3_c));  // open: dp
  BCD_to_7_segment bcd_to_7_segment_4 (
    .MSB_D3(mod10_counter_1_d3_msb), .D2(mod10_counter_1_d2), .D1(mod10_counter_1_d1),
    .LSB_D0(mod10_counter_1_d0_lsb), .A(bcd_to_7_segment_4_a), .B(bcd_to_7_segment_4_b),
    .C(bcd_to_7_segment_4_c), .D(bcd_to_7_segment_4_d), .E(bcd_to_7_segment_4_e), .F(bcd_to_7_segment_4_f),
    .G(bcd_to_7_segment_4_g));
  mod6_counter mod6_counter_1 (
    .Clk(clock_1_out), .Enable(and_2_out), .q2(mod6_counter_1_q2), .q1(mod6_counter_1_q1),
    .q0(mod6_counter_1_q0), .Z(mod6_counter_1_z));  // open: Clear
  mod10_counter mod10_counter_1 (
    .clk(clock_1_out), .enable(and_3_out), .reset(\초기화 ), .Z(mod10_counter_1_z),
    .D3_MSB(mod10_counter_1_d3_msb), .D2(mod10_counter_1_d2), .D1(mod10_counter_1_d1),
    .D0_LSB(mod10_counter_1_d0_lsb));
  and and_3 (and_3_out, mod6_counter_2_z, mod10_counter_2_z);
  Multiplexer #(.width(6)) multiplexer_1 (
    .in0(6'b000001), .in1(6'b000010), .out(multiplexer_1_out), .sel(ROUND_TRIP));  // open: en
  _7_Segment_Display u_7_segment_display_5 (
    .g(n7segmentlogic_2_g), .f(n7segmentlogic_2_f), .a(n7segmentlogic_2_a), .b(n7segmentlogic_2_b),
    .e(n7segmentlogic_2_e), .d(n7segmentlogic_2_d), .c(n7segmentlogic_2_c));  // open: dp
  _7_Segment_Display u_7_segment_display_6 (
    .g(bcd_to_7_segment_4_g), .f(bcd_to_7_segment_4_f), .a(bcd_to_7_segment_4_a), .b(bcd_to_7_segment_4_b),
    .e(bcd_to_7_segment_4_e), .d(bcd_to_7_segment_4_d), .c(bcd_to_7_segment_4_c));  // open: dp
  Multiplier #(.width(6)) multiplier_1 (
    .a(adder_1_out), .b(multiplexer_1_out), .out(multiplier_1_out));  // open: cin, cout
  Button \_100원  (.out(\_100원_out ));
  Button \_500원  (.out(\_500원_out ));
  Button \_1000원  (.out(\_1000원_out ));
  _7_Segment_Display u_7_segment_display_7 (
    .g(n7segmentlogic_3_g), .f(n7segmentlogic_3_f), .a(n7segmentlogic_3_a), .b(n7segmentlogic_3_b),
    .e(n7segmentlogic_3_e), .d(n7segmentlogic_3_d), .c(n7segmentlogic_3_c));  // open: dp
  _7segmentLogic u_7segmentlogic_2 (
    .\숫자 (divider_1_rem), .a(n7segmentlogic_2_a), .b(n7segmentlogic_2_b), .c(n7segmentlogic_2_c),
    .d(n7segmentlogic_2_d), .e(n7segmentlogic_2_e), .f(n7segmentlogic_2_f), .g(n7segmentlogic_2_g));
  _7_Segment_Display u_7_segment_display_8 (
    .g(bcd_to_7_segment_5_g), .f(bcd_to_7_segment_5_f), .a(bcd_to_7_segment_5_a), .b(bcd_to_7_segment_5_b),
    .e(bcd_to_7_segment_5_e), .d(bcd_to_7_segment_5_d), .c(bcd_to_7_segment_5_c));  // open: dp
  BCD_to_7_segment bcd_to_7_segment_5 (
    .MSB_D3(1'b0), .D2(mod6_counter_2_q2), .D1(mod6_counter_2_q1), .LSB_D0(mod6_counter_2_q0),
    .A(bcd_to_7_segment_5_a), .B(bcd_to_7_segment_5_b), .C(bcd_to_7_segment_5_c), .D(bcd_to_7_segment_5_d),
    .E(bcd_to_7_segment_5_e), .F(bcd_to_7_segment_5_f), .G(bcd_to_7_segment_5_g));
  mod6_counter mod6_counter_2 (
    .Clk(clock_1_out), .Enable(mod10_counter_2_z), .Clear(\초기화 ), .q2(mod6_counter_2_q2),
    .q1(mod6_counter_2_q1), .q0(mod6_counter_2_q0), .Z(mod6_counter_2_z));
  _7_Segment_Display u_7_segment_display_9 (
    .g(n7segmentlogic_4_g), .f(n7segmentlogic_4_f), .a(n7segmentlogic_4_a), .b(n7segmentlogic_4_b),
    .e(n7segmentlogic_4_e), .d(n7segmentlogic_4_d), .c(n7segmentlogic_4_c));  // open: dp
  Divider #(.width(6)) divider_2 (
    .a(multiplier_1_out), .b(6'b001010), .out(divider_2_out), .rem(divider_2_rem));  // open: upper
  MoneyInput MoneyInput (
    .Amount_previously_inserted(register_1_q), .in_2(\_100원_out ), .in_3(\_500원_out ), .in_4(\_1000원_out ),
    .Amount_inserted(MoneyInput_amount_inserted), .MoneyInsertCheck(MoneyInput_moneyinsertcheck));
  _7_Segment_Display u_7_segment_display_10 (
    .g(n7segmentlogic_5_g), .f(n7segmentlogic_5_f), .a(n7segmentlogic_5_a), .b(n7segmentlogic_5_b),
    .e(n7segmentlogic_5_e), .d(n7segmentlogic_5_d), .c(n7segmentlogic_5_c));  // open: dp
  _7segmentLogic u_7segmentlogic_3 (
    .\숫자 ({6{1'b0}}), .a(n7segmentlogic_3_a), .b(n7segmentlogic_3_b), .c(n7segmentlogic_3_c),
    .d(n7segmentlogic_3_d), .e(n7segmentlogic_3_e), .f(n7segmentlogic_3_f), .g(n7segmentlogic_3_g));
  _7_Segment_Display u_7_segment_display_11 (
    .g(bcd_to_7_segment_6_g), .f(bcd_to_7_segment_6_f), .a(bcd_to_7_segment_6_a), .b(bcd_to_7_segment_6_b),
    .e(bcd_to_7_segment_6_e), .d(bcd_to_7_segment_6_d), .c(bcd_to_7_segment_6_c));  // open: dp
  BCD_to_7_segment bcd_to_7_segment_6 (
    .MSB_D3(mod10_counter_2_d3_msb), .D2(mod10_counter_2_d2), .D1(mod10_counter_2_d1),
    .LSB_D0(mod10_counter_2_d0_lsb), .A(bcd_to_7_segment_6_a), .B(bcd_to_7_segment_6_b),
    .C(bcd_to_7_segment_6_c), .D(bcd_to_7_segment_6_d), .E(bcd_to_7_segment_6_e), .F(bcd_to_7_segment_6_f),
    .G(bcd_to_7_segment_6_g));
  mod10_counter mod10_counter_2 (
    .clk(clock_1_out), .enable(1'b1), .reset(\초기화 ), .Z(mod10_counter_2_z), .D3_MSB(mod10_counter_2_d3_msb),
    .D2(mod10_counter_2_d2), .D1(mod10_counter_2_d1), .D0_LSB(mod10_counter_2_d0_lsb));
  _7segmentLogic u_7segmentlogic_4 (
    .\숫자 (divider_2_out), .a(n7segmentlogic_4_a), .b(n7segmentlogic_4_b), .c(n7segmentlogic_4_c),
    .d(n7segmentlogic_4_d), .e(n7segmentlogic_4_e), .f(n7segmentlogic_4_f), .g(n7segmentlogic_4_g));
  _7segmentLogic u_7segmentlogic_5 (
    .\숫자 ({6{1'b0}}), .a(n7segmentlogic_5_a), .b(n7segmentlogic_5_b), .c(n7segmentlogic_5_c),
    .d(n7segmentlogic_5_d), .e(n7segmentlogic_5_e), .f(n7segmentlogic_5_f), .g(n7segmentlogic_5_g));
  _7_Segment_Display u_7_segment_display_12 (
    .g(n7segmentlogic_6_g), .f(n7segmentlogic_6_f), .a(n7segmentlogic_6_a), .b(n7segmentlogic_6_b),
    .e(n7segmentlogic_6_e), .d(n7segmentlogic_6_d), .c(n7segmentlogic_6_c));  // open: dp
  _7segmentLogic u_7segmentlogic_6 (
    .\숫자 (divider_2_rem), .a(n7segmentlogic_6_a), .b(n7segmentlogic_6_b), .c(n7segmentlogic_6_c),
    .d(n7segmentlogic_6_d), .e(n7segmentlogic_6_e), .f(n7segmentlogic_6_f), .g(n7segmentlogic_6_g));
  Register #(.width(6)) register_1 (
    .D(MoneyInput_amount_inserted), .Q(register_1_q), .clk(MoneyInput_moneyinsertcheck), .clr(or_1_out));  // open: en
  Multiplexer #(.width(6)) multiplexer_2 (
    .in0(in_8), .in1(divider_3_out), .out(multiplexer_2_out), .sel(MoneyRefund_balance_calculation_complete));  // open: en
  _7_Segment_Display u_7_segment_display_13 (
    .g(n7segmentlogic_8_g), .f(n7segmentlogic_8_f), .a(n7segmentlogic_8_a), .b(n7segmentlogic_8_b),
    .e(n7segmentlogic_8_e), .d(n7segmentlogic_8_d), .c(n7segmentlogic_8_c));  // open: dp
  _7_Segment_Display u_7_segment_display_14 (
    .g(n7segmentlogic_7_g), .f(n7segmentlogic_7_f), .a(n7segmentlogic_7_a), .b(n7segmentlogic_7_b),
    .e(n7segmentlogic_7_e), .d(n7segmentlogic_7_d), .c(n7segmentlogic_7_c));  // open: dp
  _7segmentLogic u_7segmentlogic_7 (
    .\숫자 ({6{1'b0}}), .a(n7segmentlogic_7_a), .b(n7segmentlogic_7_b), .c(n7segmentlogic_7_c),
    .d(n7segmentlogic_7_d), .e(n7segmentlogic_7_e), .f(n7segmentlogic_7_f), .g(n7segmentlogic_7_g));
  MoneyRefund MoneyRefund (
    .Charge(multiplier_1_out), .Input_Amount(register_1_q), .Balance(Balance),
    .Balance_calculation_complete(MoneyRefund_balance_calculation_complete));
  _7_Segment_Display u_7_segment_display_15 (
    .g(n7segmentlogic_9_g), .f(n7segmentlogic_9_f), .a(n7segmentlogic_9_a), .b(n7segmentlogic_9_b),
    .e(n7segmentlogic_9_e), .d(n7segmentlogic_9_d), .c(n7segmentlogic_9_c));  // open: dp
  _7segmentLogic u_7segmentlogic_8 (
    .\숫자 (multiplexer_2_out), .a(n7segmentlogic_8_a), .b(n7segmentlogic_8_b), .c(n7segmentlogic_8_c),
    .d(n7segmentlogic_8_d), .e(n7segmentlogic_8_e), .f(n7segmentlogic_8_f), .g(n7segmentlogic_8_g));
  _7_Segment_Display u_7_segment_display_16 (
    .g(n7segmentlogic_10_g), .f(n7segmentlogic_10_f), .a(n7segmentlogic_10_a), .b(n7segmentlogic_10_b),
    .e(n7segmentlogic_10_e), .d(n7segmentlogic_10_d), .c(n7segmentlogic_10_c));  // open: dp
  Divider #(.width(6)) divider_3 (.a(Balance), .b(6'b001010), .out(divider_3_out), .rem(divider_3_rem));  // open: upper
  _7_Segment_Display u_7_segment_display_17 (
    .g(n7segmentlogic_11_g), .f(n7segmentlogic_11_f), .a(n7segmentlogic_11_a), .b(n7segmentlogic_11_b),
    .e(n7segmentlogic_11_e), .d(n7segmentlogic_11_d), .c(n7segmentlogic_11_c));  // open: dp
  _7segmentLogic u_7segmentlogic_9 (
    .\숫자 (multiplexer_3_out), .a(n7segmentlogic_9_a), .b(n7segmentlogic_9_b), .c(n7segmentlogic_9_c),
    .d(n7segmentlogic_9_d), .e(n7segmentlogic_9_e), .f(n7segmentlogic_9_f), .g(n7segmentlogic_9_g));
  _7segmentLogic u_7segmentlogic_10 (
    .\숫자 ({6{1'b0}}), .a(n7segmentlogic_10_a), .b(n7segmentlogic_10_b), .c(n7segmentlogic_10_c),
    .d(n7segmentlogic_10_d), .e(n7segmentlogic_10_e), .f(n7segmentlogic_10_f), .g(n7segmentlogic_10_g));
  not not_1 (not_1_out, MoneyInput_moneyinsertcheck);
  not not_2 (not_2_out, MoneyRefund_balance_calculation_complete);
  Multiplexer #(.width(6)) multiplexer_3 (
    .in0(in_9), .in1(divider_3_rem), .out(multiplexer_3_out), .sel(MoneyRefund_balance_calculation_complete));  // open: en
  _7segmentLogic u_7segmentlogic_11 (
    .\숫자 ({6{1'b0}}), .a(n7segmentlogic_11_a), .b(n7segmentlogic_11_b), .c(n7segmentlogic_11_c),
    .d(n7segmentlogic_11_d), .e(n7segmentlogic_11_e), .f(n7segmentlogic_11_f), .g(n7segmentlogic_11_g));
  _7_Segment_Display u_7_segment_display_18 (
    .g(n7segmentlogic_13_g), .f(n7segmentlogic_13_f), .a(n7segmentlogic_13_a), .b(n7segmentlogic_13_b),
    .e(n7segmentlogic_13_e), .d(n7segmentlogic_13_d), .c(n7segmentlogic_13_c));  // open: dp
  Timer timer_1 (
    .\타이머_초기화 (not_1_out), .in_2(not_2_out), .\_10의_자리 (\timer_1__10의_자리 ), .\_1의_자리 (\timer_1__1의_자리 ),
    .out_5(timer_1_out_5));
  or or_1 (or_1_out, timer_1_out_5, INPUT_RESET_out);
  _7_Segment_Display u_7_segment_display_19 (
    .g(n7segmentlogic_12_g), .f(n7segmentlogic_12_f), .a(n7segmentlogic_12_a), .b(n7segmentlogic_12_b),
    .e(n7segmentlogic_12_e), .d(n7segmentlogic_12_d), .c(n7segmentlogic_12_c));  // open: dp
  _7segmentLogic u_7segmentlogic_12 (
    .\숫자 ({6{1'b0}}), .a(n7segmentlogic_12_a), .b(n7segmentlogic_12_b), .c(n7segmentlogic_12_c),
    .d(n7segmentlogic_12_d), .e(n7segmentlogic_12_e), .f(n7segmentlogic_12_f), .g(n7segmentlogic_12_g));
  _7segmentLogic u_7segmentlogic_13 (
    .\숫자 (\timer_1__10의_자리 ), .a(n7segmentlogic_13_a), .b(n7segmentlogic_13_b), .c(n7segmentlogic_13_c),
    .d(n7segmentlogic_13_d), .e(n7segmentlogic_13_e), .f(n7segmentlogic_13_f), .g(n7segmentlogic_13_g));
  Button INPUT_RESET (.out(INPUT_RESET_out));
  _7_Segment_Display u_7_segment_display_20 (
    .g(n7segmentlogic_14_g), .f(n7segmentlogic_14_f), .a(n7segmentlogic_14_a), .b(n7segmentlogic_14_b),
    .e(n7segmentlogic_14_e), .d(n7segmentlogic_14_d), .c(n7segmentlogic_14_c));  // open: dp
  _7segmentLogic u_7segmentlogic_14 (
    .\숫자 (\timer_1__1의_자리 ), .a(n7segmentlogic_14_a), .b(n7segmentlogic_14_b), .c(n7segmentlogic_14_c),
    .d(n7segmentlogic_14_d), .e(n7segmentlogic_14_e), .f(n7segmentlogic_14_f), .g(n7segmentlogic_14_g));

  // Notes on the sheet:
  //   12hour clock
  //   h
  //   INPUT AMOUNT
  //   m
  //   s
  //   CHARGE
  //   BALANCE
  //   Timer
endmodule

module MoneyInput (
  input  [5:0] Amount_previously_inserted,
  input  in_2,
  input  in_3,
  input  in_4,
  output [5:0] Amount_inserted,
  output MoneyInsertCheck
);

  wire comparator_1_lt, not_1_out;
  wire [1:0] controlled_buffer_1_out;
  wire [5:0] adder_1_out, multiplexer_1_out;

  assign controlled_buffer_1_out = MoneyInsertCheck ? 2'b00 : 2'bz;  // Controlled_Buffer controlled_buffer_1
  assign controlled_buffer_1_out = in_2 ? 2'b01 : 2'bz;  // Controlled_Buffer controlled_buffer_2
  assign controlled_buffer_1_out = in_3 ? 2'b10 : 2'bz;  // Controlled_Buffer controlled_buffer_3
  assign controlled_buffer_1_out = in_4 ? 2'b11 : 2'bz;  // Controlled_Buffer controlled_buffer_4
  Multiplexer #(.select(2), .width(6)) multiplexer_1 (
    .in0({6{1'b0}}), .in1(6'b000001), .in2(6'b000101), .in3(6'b001010), .out(multiplexer_1_out),
    .sel(controlled_buffer_1_out));  // open: en
  Adder #(.width(6)) adder_1 (
    .a(Amount_previously_inserted), .b(multiplexer_1_out), .out(adder_1_out));  // open: cin, cout
  nor nor_1 (MoneyInsertCheck, in_2, in_3, in_4);
  Comparator #(.width(6)) comparator_1 (.a(adder_1_out), .b(6'b011111), .lt(comparator_1_lt));  // open: gt, eq
  Multiplexer #(.width(6)) multiplexer_2 (
    .in0(adder_1_out), .in1(Amount_previously_inserted), .out(Amount_inserted), .sel(not_1_out));  // open: en
  not not_1 (not_1_out, comparator_1_lt);
endmodule

module MoneyRefund (
  input  [5:0] Charge,
  input  [5:0] Input_Amount,
  output [5:0] Balance,
  output Balance_calculation_complete
);

  wire comparator_1_eq, comparator_1_lt;
  wire [5:0] subtractor_1_out;

  Comparator #(.width(6)) comparator_1 (
    .a(Charge), .b(Input_Amount), .eq(comparator_1_eq), .lt(comparator_1_lt));  // open: gt
  or or_1 (Balance_calculation_complete, comparator_1_eq, comparator_1_lt);
  Subtractor #(.width(6)) subtractor_1 (.a(Input_Amount), .b(Charge), .out(subtractor_1_out));  // open: bin, bout
  Multiplexer #(.width(6)) multiplexer_1 (
    .in1(subtractor_1_out), .out(Balance), .sel(Balance_calculation_complete));  // open: in0, en
endmodule

module SelectAge (
  input  CHILD,
  input  TEEN,
  input  ADULT,
  input  SENIOR,
  output [5:0] out_5,
  output out_6
);

  wire [3:0] controlled_buffer_1_out;

  assign controlled_buffer_1_out = out_6 ? 4'b0000 : 4'bz;  // Controlled_Buffer controlled_buffer_1
  assign controlled_buffer_1_out = CHILD ? 4'b0001 : 4'bz;  // Controlled_Buffer controlled_buffer_2
  assign controlled_buffer_1_out = TEEN ? 4'b0010 : 4'bz;  // Controlled_Buffer controlled_buffer_3
  assign controlled_buffer_1_out = ADULT ? 4'b0011 : 4'bz;  // Controlled_Buffer controlled_buffer_4
  assign controlled_buffer_1_out = SENIOR ? 4'b0100 : 4'bz;  // Controlled_Buffer controlled_buffer_5
  ROM #(.addrWidth(4), .dataWidth(6)) rom_1 (.addr(controlled_buffer_1_out), .data(out_5));  // open: sel
  nor nor_1 (out_6, CHILD, TEEN, ADULT, SENIOR);

  // Notes on the sheet:
  //   contents of rom_1 (hex, n*v repeats v):
  //   0 8 a c
endmodule

module AddCharge (
  input  [3:0] DISTANCES,
  input  TRANSFER,
  output [5:0] out_3,
  output out_4
);

  wire and_1_out, and_2_out, and_3_out, and_4_out, comparator_1_gt, not_1_out, not_2_out;
  wire [3:0] controlled_buffer_1_out;

  not not_1 (not_1_out, TRANSFER);
  Comparator #(.width(4)) comparator_1 (.a(DISTANCES), .b(4'b0011), .gt(comparator_1_gt));  // open: eq, lt
  not not_2 (not_2_out, comparator_1_gt);
  and and_1 (and_1_out, not_1_out, not_2_out);
  and and_2 (and_2_out, TRANSFER, not_2_out);
  and and_3 (and_3_out, not_1_out, comparator_1_gt);
  and and_4 (and_4_out, comparator_1_gt, TRANSFER);
  assign controlled_buffer_1_out = out_4 ? 4'b0000 : 4'bz;  // Controlled_Buffer controlled_buffer_1
  assign controlled_buffer_1_out = and_1_out ? 4'b0001 : 4'bz;  // Controlled_Buffer controlled_buffer_2
  assign controlled_buffer_1_out = and_2_out ? 4'b0010 : 4'bz;  // Controlled_Buffer controlled_buffer_3
  assign controlled_buffer_1_out = and_3_out ? 4'b0011 : 4'bz;  // Controlled_Buffer controlled_buffer_4
  assign controlled_buffer_1_out = and_4_out ? 4'b0100 : 4'bz;  // Controlled_Buffer controlled_buffer_5
  ROM #(.addrWidth(4), .dataWidth(6)) rom_1 (.addr(controlled_buffer_1_out), .data(out_3));  // open: sel
  nor nor_1 (out_4, and_1_out, and_2_out, and_3_out, and_4_out);

  // Notes on the sheet:
  //   contents of rom_1 (hex, n*v repeats v):
  //   0 0 1 2 3
endmodule

module Timer (
  input  \타이머_초기화 ,
  input  in_2,
  output [5:0] \_10의_자리 ,
  output [5:0] \_1의_자리 ,
  output out_5
);

  wire and_1_out, and_2_out, clock_1_out, not_1_out;
  wire [5:0] counter_1_q, subtractor_1_out;

  Counter #(.width(6), .max('h3c)) counter_1 (
    .Q(counter_1_q), .clk(and_1_out), .clr(\타이머_초기화 ));  // open: load, D, count, carry
  and and_1 (and_1_out, clock_1_out, and_2_out);
  Clock clock_1 (.out(clock_1_out));
  and and_2 (and_2_out, not_1_out, in_2);
  Subtractor #(.width(6)) subtractor_1 (.a(6'b111100), .b(counter_1_q), .out(subtractor_1_out));  // open: bin, bout
  not not_1 (not_1_out, out_5);
  Comparator #(.width(6)) comparator_1 (.a(subtractor_1_out), .b({6{1'b0}}), .eq(out_5));  // open: gt, lt
  Divider #(.width(6)) divider_1 (.a(subtractor_1_out), .b(6'b001010), .out(\_10의_자리 ), .rem(\_1의_자리 ));  // open: upper
endmodule

module _7segmentLogic (
  input  [5:0] \숫자 ,
  output a,
  output d,
  output e,
  output f,
  output g,
  output b,
  output c
);

  wire comparator_1_eq, comparator_2_eq, comparator_3_eq, comparator_4_eq, comparator_5_eq, comparator_6_eq,
       comparator_7_eq, comparator_8_eq, comparator_9_eq, comparator_10_eq;

  or or_1 (a, comparator_4_eq, comparator_8_eq, comparator_1_eq, comparator_3_eq, comparator_6_eq, comparator_7_eq, comparator_9_eq, comparator_10_eq);
  Comparator #(.width(6)) comparator_1 (.a(\숫자 ), .b({6{1'b0}}), .eq(comparator_1_eq));  // open: gt, lt
  or or_2 (b, comparator_3_eq, comparator_8_eq, comparator_1_eq, comparator_2_eq, comparator_4_eq, comparator_5_eq, comparator_9_eq, comparator_10_eq);
  Comparator #(.width(6)) comparator_2 (.a(\숫자 ), .b(6'b000001), .eq(comparator_2_eq));  // open: gt, lt
  or or_3 (c, comparator_8_eq, comparator_9_eq, comparator_1_eq, comparator_2_eq, comparator_4_eq, comparator_5_eq, comparator_6_eq, comparator_7_eq, comparator_10_eq);
  Comparator #(.width(6)) comparator_3 (.a(\숫자 ), .b(6'b000010), .eq(comparator_3_eq));  // open: gt, lt
  or or_4 (d, comparator_9_eq, comparator_1_eq, comparator_3_eq, comparator_4_eq, comparator_6_eq, comparator_7_eq, comparator_10_eq);
  Comparator #(.width(6)) comparator_4 (.a(\숫자 ), .b(6'b000011), .eq(comparator_4_eq));  // open: gt, lt
  or or_5 (e, comparator_1_eq, comparator_3_eq, comparator_7_eq, comparator_9_eq);
  Comparator #(.width(6)) comparator_5 (.a(\숫자 ), .b(6'b000100), .eq(comparator_5_eq));  // open: gt, lt
  Comparator #(.width(6)) comparator_6 (.a(\숫자 ), .b(6'b000101), .eq(comparator_6_eq));  // open: gt, lt
  or or_6 (f, comparator_6_eq, comparator_1_eq, comparator_5_eq, comparator_7_eq, comparator_9_eq, comparator_10_eq);
  Comparator #(.width(6)) comparator_7 (.a(\숫자 ), .b(6'b000110), .eq(comparator_7_eq));  // open: gt, lt
  or or_7 (g, comparator_9_eq, comparator_3_eq, comparator_4_eq, comparator_5_eq, comparator_6_eq, comparator_7_eq, comparator_10_eq);
  Comparator #(.width(6)) comparator_8 (.a(\숫자 ), .b(6'b000111), .eq(comparator_8_eq));  // open: gt, lt
  Comparator #(.width(6)) comparator_9 (.a(\숫자 ), .b(6'b001000), .eq(comparator_9_eq));  // open: gt, lt
  Comparator #(.width(6)) comparator_10 (.a(\숫자 ), .b(6'b001001), .eq(comparator_10_eq));  // open: gt, lt
endmodule

module _12hour_clock (
  input  \초기화 
);

  wire and_1_out, and_2_out, and_3_out, bcd_to_7_segment_1_a, bcd_to_7_segment_1_b, bcd_to_7_segment_1_c,
       bcd_to_7_segment_1_d, bcd_to_7_segment_1_e, bcd_to_7_segment_1_f, bcd_to_7_segment_1_g,
       bcd_to_7_segment_2_a, bcd_to_7_segment_2_b, bcd_to_7_segment_2_c, bcd_to_7_segment_2_d,
       bcd_to_7_segment_2_e, bcd_to_7_segment_2_f, bcd_to_7_segment_2_g, bcd_to_7_segment_3_a,
       bcd_to_7_segment_3_b, bcd_to_7_segment_3_c, bcd_to_7_segment_3_d, bcd_to_7_segment_3_e,
       bcd_to_7_segment_3_f, bcd_to_7_segment_3_g, bcd_to_7_segment_4_a, bcd_to_7_segment_4_b,
       bcd_to_7_segment_4_c, bcd_to_7_segment_4_d, bcd_to_7_segment_4_e, bcd_to_7_segment_4_f,
       bcd_to_7_segment_4_g, bcd_to_7_segment_5_a, bcd_to_7_segment_5_b, bcd_to_7_segment_5_c,
       bcd_to_7_segment_5_d, bcd_to_7_segment_5_e, bcd_to_7_segment_5_f, bcd_to_7_segment_5_g,
       bcd_to_7_segment_6_a, bcd_to_7_segment_6_b, bcd_to_7_segment_6_c, bcd_to_7_segment_6_d,
       bcd_to_7_segment_6_e, bcd_to_7_segment_6_f, bcd_to_7_segment_6_g, clock_1_out, mod6_counter_1_q0,
       mod6_counter_1_q1, mod6_counter_1_q2, mod6_counter_1_z, mod6_counter_2_q0, mod6_counter_2_q1,
       mod6_counter_2_q2, mod6_counter_2_z, mod10_counter_1_d0_lsb, mod10_counter_1_d1, mod10_counter_1_d2,
       mod10_counter_1_d3_msb, mod10_counter_1_z, mod10_counter_2_d0_lsb, mod10_counter_2_d1,
       mod10_counter_2_d2, mod10_counter_2_d3_msb, mod10_counter_2_z, n12h_counter_1_a0, n12h_counter_1_b0,
       n12h_counter_1_b1, n12h_counter_1_b2, n12h_counter_1_b3;

  _7_Segment_Display u_7_segment_display_1 (
    .g(bcd_to_7_segment_1_g), .f(bcd_to_7_segment_1_f), .a(bcd_to_7_segment_1_a), .b(bcd_to_7_segment_1_b),
    .e(bcd_to_7_segment_1_e), .d(bcd_to_7_segment_1_d), .c(bcd_to_7_segment_1_c));  // open: dp
  BCD_to_7_segment bcd_to_7_segment_1 (
    .MSB_D3(1'b0), .D2(1'b0), .D1(1'b0), .LSB_D0(n12h_counter_1_a0), .A(bcd_to_7_segment_1_a),
    .B(bcd_to_7_segment_1_b), .C(bcd_to_7_segment_1_c), .D(bcd_to_7_segment_1_d), .E(bcd_to_7_segment_1_e),
    .F(bcd_to_7_segment_1_f), .G(bcd_to_7_segment_1_g));
  _7_Segment_Display u_7_segment_display_2 (
    .g(bcd_to_7_segment_2_g), .f(bcd_to_7_segment_2_f), .a(bcd_to_7_segment_2_a), .b(bcd_to_7_segment_2_b),
    .e(bcd_to_7_segment_2_e), .d(bcd_to_7_segment_2_d), .c(bcd_to_7_segment_2_c));  // open: dp
  BCD_to_7_segment bcd_to_7_segment_2 (
    .MSB_D3(n12h_counter_1_b3), .D2(n12h_counter_1_b2), .D1(n12h_counter_1_b1), .LSB_D0(n12h_counter_1_b0),
    .A(bcd_to_7_segment_2_a), .B(bcd_to_7_segment_2_b), .C(bcd_to_7_segment_2_c), .D(bcd_to_7_segment_2_d),
    .E(bcd_to_7_segment_2_e), .F(bcd_to_7_segment_2_f), .G(bcd_to_7_segment_2_g));
  _12h_counter u_12h_counter_1 (
    .Clk(clock_1_out), .Enable(and_1_out), .Clear(\초기화 ), .A0(n12h_counter_1_a0), .B0(n12h_counter_1_b0),
    .B1(n12h_counter_1_b1), .B2(n12h_counter_1_b2), .B3(n12h_counter_1_b3));
  and and_1 (and_1_out, mod6_counter_1_z, and_2_out);
  Clock clock_1 (.out(clock_1_out));
  BCD_to_7_segment bcd_to_7_segment_3 (
    .MSB_D3(1'b0), .D2(mod6_counter_1_q2), .D1(mod6_counter_1_q1), .LSB_D0(mod6_counter_1_q0),
    .A(bcd_to_7_segment_3_a), .B(bcd_to_7_segment_3_b), .C(bcd_to_7_segment_3_c), .D(bcd_to_7_segment_3_d),
    .E(bcd_to_7_segment_3_e), .F(bcd_to_7_segment_3_f), .G(bcd_to_7_segment_3_g));
  and and_2 (and_2_out, mod10_counter_1_z, and_3_out);
  _7_Segment_Display u_7_segment_display_3 (
    .g(bcd_to_7_segment_3_g), .f(bcd_to_7_segment_3_f), .a(bcd_to_7_segment_3_a), .b(bcd_to_7_segment_3_b),
    .e(bcd_to_7_segment_3_e), .d(bcd_to_7_segment_3_d), .c(bcd_to_7_segment_3_c));  // open: dp
  BCD_to_7_segment bcd_to_7_segment_4 (
    .MSB_D3(mod10_counter_1_d3_msb), .D2(mod10_counter_1_d2), .D1(mod10_counter_1_d1),
    .LSB_D0(mod10_counter_1_d0_lsb), .A(bcd_to_7_segment_4_a), .B(bcd_to_7_segment_4_b),
    .C(bcd_to_7_segment_4_c), .D(bcd_to_7_segment_4_d), .E(bcd_to_7_segment_4_e), .F(bcd_to_7_segment_4_f),
    .G(bcd_to_7_segment_4_g));
  mod6_counter mod6_counter_1 (
    .Clk(clock_1_out), .Enable(and_2_out), .q2(mod6_counter_1_q2), .q1(mod6_counter_1_q1),
    .q0(mod6_counter_1_q0), .Z(mod6_counter_1_z));  // open: Clear
  mod10_counter mod10_counter_1 (
    .clk(clock_1_out), .enable(and_3_out), .reset(\초기화 ), .Z(mod10_counter_1_z),
    .D3_MSB(mod10_counter_1_d3_msb), .D2(mod10_counter_1_d2), .D1(mod10_counter_1_d1),
    .D0_LSB(mod10_counter_1_d0_lsb));
  and and_3 (and_3_out, mod6_counter_2_z, mod10_counter_2_z);
  _7_Segment_Display u_7_segment_display_4 (
    .g(bcd_to_7_segment_4_g), .f(bcd_to_7_segment_4_f), .a(bcd_to_7_segment_4_a), .b(bcd_to_7_segment_4_b),
    .e(bcd_to_7_segment_4_e), .d(bcd_to_7_segment_4_d), .c(bcd_to_7_segment_4_c));  // open: dp
  _7_Segment_Display u_7_segment_display_5 (
    .g(bcd_to_7_segment_5_g), .f(bcd_to_7_segment_5_f), .a(bcd_to_7_segment_5_a), .b(bcd_to_7_segment_5_b),
    .e(bcd_to_7_segment_5_e), .d(bcd_to_7_segment_5_d), .c(bcd_to_7_segment_5_c));  // open: dp
  BCD_to_7_segment bcd_to_7_segment_5 (
    .MSB_D3(1'b0), .D2(mod6_counter_2_q2), .D1(mod6_counter_2_q1), .LSB_D0(mod6_counter_2_q0),
    .A(bcd_to_7_segment_5_a), .B(bcd_to_7_segment_5_b), .C(bcd_to_7_segment_5_c), .D(bcd_to_7_segment_5_d),
    .E(bcd_to_7_segment_5_e), .F(bcd_to_7_segment_5_f), .G(bcd_to_7_segment_5_g));
  mod6_counter mod6_counter_2 (
    .Clk(clock_1_out), .Enable(mod10_counter_2_z), .Clear(\초기화 ), .q2(mod6_counter_2_q2),
    .q1(mod6_counter_2_q1), .q0(mod6_counter_2_q0), .Z(mod6_counter_2_z));
  _7_Segment_Display u_7_segment_display_6 (
    .g(bcd_to_7_segment_6_g), .f(bcd_to_7_segment_6_f), .a(bcd_to_7_segment_6_a), .b(bcd_to_7_segment_6_b),
    .e(bcd_to_7_segment_6_e), .d(bcd_to_7_segment_6_d), .c(bcd_to_7_segment_6_c));  // open: dp
  BCD_to_7_segment bcd_to_7_segment_6 (
    .MSB_D3(mod10_counter_2_d3_msb), .D2(mod10_counter_2_d2), .D1(mod10_counter_2_d1),
    .LSB_D0(mod10_counter_2_d0_lsb), .A(bcd_to_7_segment_6_a), .B(bcd_to_7_segment_6_b),
    .C(bcd_to_7_segment_6_c), .D(bcd_to_7_segment_6_d), .E(bcd_to_7_segment_6_e), .F(bcd_to_7_segment_6_f),
    .G(bcd_to_7_segment_6_g));
  mod10_counter mod10_counter_2 (
    .clk(clock_1_out), .enable(1'b1), .reset(\초기화 ), .Z(mod10_counter_2_z), .D3_MSB(mod10_counter_2_d3_msb),
    .D2(mod10_counter_2_d2), .D1(mod10_counter_2_d1), .D0_LSB(mod10_counter_2_d0_lsb));

  // Notes on the sheet:
  //   12hour clock
  //   h
  //   m
  //   s
endmodule

module _12h_counter (
  input  Clk,
  input  Enable,
  input  Clear,
  output A0,
  output B0,
  output B1,
  output B2,
  output B3
);

  wire and_1_out, and_2_out, and_3_out, and_4_out, and_5_out, and_6_out, and_8_out, and_9_out, and_10_out,
       and_11_out, d_ff_1_q, d_ff_1_qn, d_ff_2_qn, d_ff_3_q, d_ff_3_qn, d_ff_4_qn, or_1_out, or_2_out,
       xor_1_out;

  or or_1 (or_1_out, and_2_out, and_3_out, and_1_out);
  and and_1 (and_1_out, d_ff_4_qn, d_ff_1_q);
  and and_2 (and_2_out, B2, d_ff_3_q, B0);
  and and_3 (and_3_out, d_ff_3_qn, d_ff_1_q);
  D_Flip_Flop d_ff_1 (.clk(Clk), .D(or_1_out), .Q(d_ff_1_q), .Qn(d_ff_1_qn), .preset(1'b0), .en(Enable), .reset(Clear));
  or or_2 (or_2_out, and_4_out, and_5_out, and_6_out);
  and and_4 (and_4_out, d_ff_1_qn, d_ff_2_qn, d_ff_3_q, B0);
  and and_5 (and_5_out, B2, d_ff_4_qn);
  and and_6 (and_6_out, B2, d_ff_3_qn);
  D_Flip_Flop d_ff_2 (.clk(Clk), .D(or_2_out), .Q(B2), .Qn(d_ff_2_qn), .preset(1'b0), .en(Enable), .reset(Clear));
  xor xor_1 (xor_1_out, B0, d_ff_3_q);
  D_Flip_Flop d_ff_3 (
    .clk(Clk), .D(xor_1_out), .Q(d_ff_3_q), .Qn(d_ff_3_qn), .preset(1'b0), .en(Enable), .reset(Clear));
  D_Flip_Flop d_ff_4 (.clk(Clk), .D(d_ff_4_qn), .Q(B0), .Qn(d_ff_4_qn), .preset(1'b0), .en(Enable), .reset(Clear));
  and and_7 (B3, d_ff_1_q, d_ff_3_qn);
  and and_8 (and_8_out, d_ff_1_qn, d_ff_2_qn, d_ff_3_qn, d_ff_4_qn);
  and and_9 (and_9_out, d_ff_1_q, d_ff_3_q);
  and and_10 (and_10_out, d_ff_1_qn, d_ff_2_qn, d_ff_4_qn);
  and and_11 (and_11_out, d_ff_1_qn, d_ff_3_q);
  or or_3 (A0, and_8_out, and_9_out);
  or or_4 (B1, and_10_out, and_11_out);

  // Notes on the sheet:
  //   D3
  //   D2
  //   D1
  //   D0
endmodule

// mod10
module mod10_counter (
  input  clk,
  input  enable,
  input  reset,
  output Z,
  output D3_MSB,
  output D2,
  output D1,
  output D0_LSB
);

  wire and_2_out, and_3_out, and_4_out, and_5_out, j_k_ff_1_qn, not_1_out, not_2_out;

  and and_1 (Z, D3_MSB, not_2_out, not_1_out, D0_LSB);
  not not_1 (not_1_out, D1);
  not not_2 (not_2_out, D2);
  and and_2 (and_2_out, D2, D1, D0_LSB);
  J_K_Flip_Flop j_k_ff_1 (
    .J(and_2_out), .clk(clk), .K(D0_LSB), .Q(D3_MSB), .Qn(j_k_ff_1_qn), .preset(1'b0), .en(enable),
    .reset(reset));
  and and_3 (and_3_out, D1, D0_LSB);
  J_K_Flip_Flop j_k_ff_2 (
    .J(and_3_out), .clk(clk), .K(and_5_out), .Q(D2), .preset(1'b0), .en(enable), .reset(reset));  // open: Qn
  and and_4 (and_4_out, j_k_ff_1_qn, D0_LSB);
  J_K_Flip_Flop j_k_ff_3 (
    .J(and_4_out), .clk(clk), .K(D0_LSB), .Q(D1), .preset(1'b0), .en(enable), .reset(reset));  // open: Qn
  and and_5 (and_5_out, D1, D0_LSB);
  J_K_Flip_Flop j_k_ff_4 (
    .J(1'b1), .clk(clk), .K(1'b1), .Q(D0_LSB), .preset(1'b0), .en(enable), .reset(reset));  // open: Qn
endmodule

module mod6_counter (
  input  Clk,
  input  Enable,
  input  Clear,
  output q2,
  output q1,
  output q0,
  output Z
);

  wire and_1_out, and_2_out, j_k_ff_1_qn;

  and and_1 (and_1_out, q0, q1);
  J_K_Flip_Flop j_k_ff_1 (
    .J(and_1_out), .clk(Clk), .K(q0), .Q(q2), .Qn(j_k_ff_1_qn), .preset(1'b0), .en(Enable), .reset(Clear));
  J_K_Flip_Flop j_k_ff_2 (
    .J(and_2_out), .clk(Clk), .K(q0), .Q(q1), .preset(1'b0), .en(Enable), .reset(Clear));  // open: Qn
  and and_2 (and_2_out, j_k_ff_1_qn, q0);
  J_K_Flip_Flop j_k_ff_3 (
    .J(1'b1), .clk(Clk), .K(1'b1), .Q(q0), .preset(1'b0), .en(Enable), .reset(Clear));  // open: Qn
  and and_3 (Z, q2, q0);
endmodule

// BCD-7seg.
module BCD_to_7_segment (
  input  MSB_D3,
  input  D2,
  input  D1,
  input  LSB_D0,
  output A,
  output B,
  output C,
  output D,
  output E,
  output F,
  output G
);

  wire and_1_out, and_2_out, and_3_out, and_4_out, and_5_out, and_6_out, and_7_out, and_8_out, and_9_out,
       and_10_out, not_1_out, not_2_out, not_3_out, not_4_out, not_5_out, not_6_out, not_7_out, not_8_out,
       not_9_out, not_10_out, not_11_out, xnor_1_out, xnor_2_out, xor_1_out;

  not not_1 (not_1_out, LSB_D0);
  not not_2 (not_2_out, D1);
  not not_3 (not_3_out, D2);
  not not_4 (not_4_out, LSB_D0);
  not not_5 (not_5_out, D2);
  not not_6 (not_6_out, LSB_D0);
  not not_7 (not_7_out, D2);
  not not_8 (not_8_out, D1);
  not not_9 (not_9_out, D2);
  not not_10 (not_10_out, LSB_D0);
  xnor xnor_1 (xnor_1_out, D2, LSB_D0);
  xnor xnor_2 (xnor_2_out, D1, LSB_D0);
  and and_1 (and_1_out, D1, not_4_out);
  and and_2 (and_2_out, not_5_out, not_6_out);
  and and_3 (and_3_out, not_7_out, D1);
  and and_4 (and_4_out, not_8_out, D2, LSB_D0);
  and and_5 (and_5_out, not_9_out, not_1_out);
  and and_6 (and_6_out, not_1_out, D1);
  and and_7 (and_7_out, not_1_out, D2);
  and and_8 (and_8_out, not_1_out, not_2_out);
  and and_9 (and_9_out, D2, not_2_out);
  xor xor_1 (xor_1_out, D1, D2);
  and and_10 (and_10_out, not_10_out, D1);
  not not_11 (not_11_out, D1);
  or or_1 (A, MSB_D3, xnor_1_out, D1);
  or or_2 (B, xnor_2_out, not_3_out);
  or or_3 (C, D2, not_11_out, LSB_D0);
  or or_4 (D, MSB_D3, and_1_out, and_2_out, and_3_out, and_4_out);
  or or_5 (E, and_5_out, and_6_out);
  or or_6 (F, and_7_out, MSB_D3, and_8_out, and_9_out);
  or or_7 (G, MSB_D3, xor_1_out, and_10_out);
endmodule
